# Fritzing sketch breadboard_schematic (saved by Fritzing 1.0.2b)
breadboards: 1

parts:
  74HC595_1 = 74HC595 [package="DIP16 [THT]"]
  AT28C16 = IC, DIP package, 24 pins [chip_label=28C16]
  74HC595_2 = 74HC595 [package="DIP16 [THT]"]
  J1 = NUCLEO-F303K8  # not connected

nets:
  N1: 74HC595_1.Q5, AT28C16.pin19
  N2: 74HC595_1.Q6, AT28C16.pin22
  N3: 74HC595_1.Q7, AT28C16.pin23
  GND: 74HC595_1.GND, 74HC595_1.OE, AT28C16.pin12, AT28C16.pin18, 74HC595_2.GND, 74HC595_2.OE
  N4: 74HC595_1.Q7', 74HC595_2.DS
  5V: 74HC595_1.MR, 74HC595_1.VCC, AT28C16.pin24, 74HC595_2.MR, 74HC595_2.VCC
  N5: 74HC595_1.SH_CP, 74HC595_2.SH_CP
  N6: 74HC595_1.ST_CP, 74HC595_2.ST_CP
  N7: AT28C16.pin1, 74HC595_2.Q0
  N8: AT28C16.pin2, 74HC595_2.Q1
  N9: AT28C16.pin3, 74HC595_2.Q2
  N10: AT28C16.pin4, 74HC595_2.Q3
  N11: AT28C16.pin5, 74HC595_2.Q4
  N12: AT28C16.pin6, 74HC595_2.Q5
  N13: AT28C16.pin7, 74HC595_2.Q6
  N14: AT28C16.pin8, 74HC595_2.Q7

custom parts:
  NUCLEO-F303K8: The highly affordable STM32 Nucleo boards allow to try out new ideas and to quickly create prototypes with any STM32 MCU. Sharing Arduino connectors and ST Morpho headers, STM32 Nucleo boards can easily be extended with a large number of application related hardware add-ons. The STM32 Nucleo boards come with an integrated ST-Link debugger/programmer; no need for an external probe. The boards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
